# Fritzing sketch sketsa_straight_cable_GSM (saved by Fritzing 0.9.10b)
breadboards: 1

parts:
  NodeMCU_v1 = NodeMCU v3 LoLin [part_number=ESP8266]
  DHT1 = DHT22 Humidity and Temperature Sensor
  U1 = LM2596 step down module
  Grove1 = Grove Dust Sensor
  M1 = sim800L v2 evb
  JACK1 = 2.1mm Barrel Jack with Terminal Block

nets:
  N1: NodeMCU_v1.D3, M1.pin_4
  N2: NodeMCU_v1.D4, M1.pin_3
  GND: NodeMCU_v1.GND, DHT1.GND, U1.IN-, U1.OUT-, Grove1.GND, M1.pin_2, M1.pin_5, M1.pin_6, JACK1.NEG
  N3: NodeMCU_v1.D5, Grove1.SIG
  N4: NodeMCU_v1.D6, Grove1.NC
  N5: NodeMCU_v1.D7, DHT1.DATA
  3V3: NodeMCU_v1.3V3, DHT1.VDD
  VIN: NodeMCU_v1.VIN, U1.OUT+, Grove1.VCC, M1.pin_7
  N6: U1.IN+, JACK1.POS

notes:
  Change to 5V

custom parts:
  NodeMCU v3 LoLin: NodeMCU v3 LoLin NodeMCU (http://www.nodemcu.com/) is an open source IoT platform. It includes firmware (https://nodemcu-build.com/) which runs on the ESP8266 Wi-Fi SoC from Espressif Systems, and hardware which is based on the ESP-12E module. The term "NodeMCU" by default refers to the firmware rather than the dev kits. The firmware uses the Lua scripting language. It is based on the eLua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
  LM2596 step down module: LM2596 DC-DC step down power supply module 3 A.
  Grove Dust Sensor: PPD42 Grove Dust Sensor
  sim800L v2 evb: sim800L v2 evb GSM module.
